# Fritzing sketch ComputerHeatMonitor (saved by Fritzing 0.9.3b)
breadboards: 1

parts:
  R1 = Resistor [tolerance=±5% resistance=330 package=THT]
  R2 = Resistor [tolerance=±5% resistance=330 package=THT]
  R3 = Resistor [tolerance=±5% resistance=330 package=THT]
  LED1 = RGB LED (com. cathode, rgb) [package="5 mm [THT]"]
  Parça1 = Arduino Uno (Rev3)
  T1 = LM35 Temperature Sensor [package="TO92 [THT]"]
  R4 = Resistor [tolerance=±5% resistance=100 package=THT]
  R5 = Resistor [tolerance=±5% resistance=100 package=THT]
  R6 = Resistor [tolerance=±5% resistance=100 package=THT]
  BT1 = Bluetooth HC-06d [package=THT]

nets:
  N1: R1.Pin_0, Parça1.D5_PWM
  N2: R1.Pin_1, LED1.blue_anode
  N3: R2.Pin_0, Parça1.D6_PWM
  N4: R2.Pin_1, LED1.green_anode
  N5: R3.Pin_0, Parça1.D7
  N6: R3.Pin_1, LED1.red_anode
  GND: LED1.common_cathode, Parça1.GND, T1.GND, R5.Pin_1, BT1.GND
  N7: Parça1.A0, T1.Vout
  N8: Parça1.D10_PWM/SS, R6.Pin_0
  N9: Parça1.D11_PWM/MOSI, BT1.TXD
  5V: Parça1.5V, T1.+Vs, BT1.VCC
  N10: R4.Pin_0, R6.Pin_1, BT1.RXD
  N11: R4.Pin_1, R5.Pin_0

custom parts:
  Bluetooth HC-06d: Bluetooth HC-06 - face down, pins down 16.5mm x 37.5mm PCB
